# Fritzing sketch diagram (saved by Fritzing 0.9.10b)

parts:
  LCD2004-I2C1 = LCD2004-I2C
  ZS-042_RTC1 = ZS-042 RTC Module
  microSD1 = MicroSD Card Module
  BAT1 = 18650 battery holder [package=battery-18650-kit]
  BAT2 = 18650 battery holder [package=battery-18650-kit]
  BAT3 = 18650 battery holder [package=battery-18650-kit]
  BAT4 = 18650 battery holder [package=battery-18650-kit]
  Mod1 = Voltage Sensor 25V
  Part2 = ACS712 Current Sensor 5A 20A 30A
  J2 = female pin header, 2 pins [form="♀ (female)"]
  J3 = female pin header, 2 pins [form="♀ (female)"]
  J6 = female pin header, 2 pins [form="♀ (female)"]
  J7 = female pin header, 2 pins [form="♀ (female)"]
  Part3 = Arduino Mega 2560 (Rev3)
  J8 = female pin header, 2 pins [form="♀ (female)"]
  8_Channel_Relay1 = 8 Channel Power Relay
  J9 = female pin header, 2 pins [form="♀ (female)"]
  Mod2 = 3S-BMS
  J10 = female pin header, 2 pins [form="♀ (female)"]
  J11 = female pin header, 2 pins [form="♀ (female)"]

nets:
  N1: LCD2004-I2C1.GND, J2.pin1
  N2: LCD2004-I2C1.VCC, J2.pin2
  N3: LCD2004-I2C1.SDA, ZS-042_RTC1.SDA, Part3.D20/SDA
  N4: LCD2004-I2C1.SCL, ZS-042_RTC1.SCL, Part3.D21/SCL
  N5: ZS-042_RTC1.GND, J3.pin1
  N6: ZS-042_RTC1.VCC, J3.pin2
  N7: microSD1.GND, J8.pin1
  N8: microSD1.VCC, J8.pin2
  N9: microSD1.MISO, Part3.D48
  N10: microSD1.MOSI, Part3.D49
  N11: microSD1.SCK, Part3.D50
  N12: microSD1.CS, Part3.D51
  N13: BAT1.+, BAT2.-, 8_Channel_Relay1.COM#25, Mod2.4.2V
  N14: BAT1.-, 8_Channel_Relay1.COM#22, Mod2.0V
  N15: BAT2.+, BAT3.-, 8_Channel_Relay1.COM#28, Mod2.8.4V
  N16: BAT3.+, BAT4.-, 8_Channel_Relay1.COM#31, J11.pin1
  N17: BAT4.+, 8_Channel_Relay1.COM#34, Mod2.12.6V
  N18: Mod1.GND, Mod1.-, J7.pin2
  N19: Mod1.S, Part3.A1
  N20: Mod1.+, J7.pin1
  N21: Part2.2, Part2.OUT, Part3.A0
  N22: Part2.VCC, J6.pin1
  N23: Part2.GND, J6.pin2
  N24: Part3.D22, 8_Channel_Relay1.IN1
  N25: Part3.D24, 8_Channel_Relay1.IN2
  N26: Part3.D26, 8_Channel_Relay1.IN3
  N27: Part3.D28, 8_Channel_Relay1.IN4
  N28: Part3.D30, 8_Channel_Relay1.IN5
  N29: Part3.D32, 8_Channel_Relay1.IN6
  N30: Part3.D34, 8_Channel_Relay1.IN7
  N31: Part3.D36, 8_Channel_Relay1.IN8
  N32: 8_Channel_Relay1.GND, J9.pin1
  N33: 8_Channel_Relay1.VCC, J9.pin2
  N34: Mod2.-, J10.pin1
  N35: Mod2.+, J10.pin2

custom parts:
  LCD2004-I2C: A standard character display with 4x20 characters. Comes in many colors with LCM2004 IIC attached.
  18650 battery holder: 18650 Battery Holder
  ACS712 Current Sensor 5A 20A 30A: Remix by Michael Kubina http://www.kubina.info Original by: https://forum.fritzing.org/t/current-sensor-5a-acs712/7694 https://forum.fritzing.org/u/ArtHome ArtHome12@gmail.com
  8 Channel Power Relay: An 8 channel power relay. The module operates at 5V.
  3S-BMS: 3S-BMS LIPO battery charger / protection unit. Note pcb does not match the board as it will likely connect with wires, so pcb is 6 pads suitable for .1in header pins.
